# Fritzing sketch hx711_spi (saved by Fritzing 0.9.3b)

parts:
  Raspberry_Pi_1 = Raspberry Pi 3 [part_number=RPI-3-V1.2]
  Part1 = HX711 Weighing Sensor Module

nets:
  3V3: Raspberry_Pi_1.3v3, Part1.VCC
  N1: Raspberry_Pi_1.GIPO10, Part1.CK/TX
  N2: Raspberry_Pi_1.GIPO9, Part1.DO/RX
  GND: Raspberry_Pi_1.GND, Part1.GND

notes:
  CK / TX connected to MOSI
